# Fritzing sketch schematic (saved by Fritzing 0.9.2b)
breadboards: 1

parts:
  Part1 = Photon
  RHT1 = Humidity and Temperature Sensor RHT03
  PIR1 = PIR sensor
  R1 = Resistor [tolerance=±5% resistance=4.7k package="0805 [SMD]"]

nets:
  N1: Part1.A0, PIR1.SIG, R1.Pin_0
  GND: Part1.GND, RHT1.GND_1, PIR1.GND, R1.Pin_1
  VIN: Part1.VIN, PIR1.VDD
  N2: Part1.D0, RHT1.Data-signal
  3V3: Part1.3V3, RHT1.Vcc
